# Fritzing sketch Untitled Sketch 2 (saved by Fritzing 0.8.3b)
breadboards: 1

parts:
  Raspberry_Pi_rev1 = Raspberry Pi rev2
  LED1 = LED - 5mm [color="Red (633nm)" package="5 mm [THT]"]
  R1 = Resistor [tolerance=±5% resistance=220 package=THT]

nets:
  N1: Raspberry_Pi_rev1.GND, LED1.cathode
  N2: Raspberry_Pi_rev1.GPIO_23, R1.Pin_1
  N3: LED1.anode, R1.Pin_0
